# Fritzing sketch controller (saved by Fritzing 0.9.3b)

parts:
  Componente5 = Arduino Uno (Rev3)
  Componente6 = Arduino Mega 2560 (Rev3)
  M2 = Niren can bus module [package=THT]

nets:
  N1: Componente5.5V, M2.pin1
  N2: Componente6.D21/SCL, M2.pin7
  N3: Componente6.D50, M2.pin4
  N4: Componente6.D51, M2.pin5
  N5: Componente6.D52, M2.pin6
  N6: Componente6.D53, M2.pin3
  N7: Componente6.GND, M2.pin2
  N8: M2.pin8, M2.pin9

custom parts:
  Niren can bus module: Niren can bus module availabe on ebay and others. Pcb view assumes that you unsolder the 7 pin header and resolder it on the bottom of the module to connect to the pcb. The two jumpers and the can bus connector remain on the top of the board and don't appear in pcb view.
