# Fritzing sketch node1 (saved by Fritzing 0.9.3b)

parts:
  Componente6 = Arduino Uno (Rev3)
  R8 = Resistor [tolerance=±5% resistance=680k package=THT]
  C4 = Electrolytic Capacitor [capacitance=47µF package="100 mil [THT, electrolytic]"]
  LED4 = LED - 5mm [color="Red (633nm)" package="5 mm [THT]"]
  R9 = Resistor [tolerance=±5% resistance=220 package=THT]
  R10 = Resistor [tolerance=±5% resistance=220 package=THT]
  M3 = Niren can bus module [package=THT]
  R11 = TRIMPOT [package=3386u]
  LED5 = LED - 5mm [color="Green (565nm)" package="5 mm [THT]"]

nets:
  N1: Componente6.A0, R11.WIPER
  N2: Componente6.A1, R8.Pin_0, C4.+
  N3: Componente6.D10_PWM/SS, M3.pin3
  N4: Componente6.D11_PWM/MOSI, M3.pin5
  N5: Componente6.D12/MISO, M3.pin4
  N6: Componente6.D13/SCK, M3.pin6
  N7: Componente6.GND, C4.-, LED4.cathode, M3.pin2, R11.CCW, LED5.cathode
  N8: Componente6.D2, M3.pin7
  N9: Componente6.D3_PWM, R10.Pin_1
  N10: Componente6.D4, R9.Pin_1
  N11: Componente6.D5_PWM, R8.Pin_1
  N12: Componente6.5V, M3.pin1, R11.CW
  N13: LED4.anode, R10.Pin_0
  N14: R9.Pin_0, LED5.anode
  N15: M3.pin8, M3.pin9

custom parts:
  Niren can bus module: Niren can bus module availabe on ebay and others. Pcb view assumes that you unsolder the 7 pin header and resolder it on the bottom of the module to connect to the pcb. The two jumpers and the can bus connector remain on the top of the board and don't appear in pcb view.
