# Fritzing sketch node2 (saved by Fritzing 0.9.3b)

parts:
  LED10 = LED - 5mm [color="Blue (505nm)" package="5 mm [THT]"]
  R17 = Resistor [tolerance=±5% resistance=220 package=THT]
  R18 = Resistor [tolerance=±5% resistance=220 package=THT]
  M5 = Niren can bus module [package=THT]
  R19 = TRIMPOT [package=3386u]
  LED11 = LED - 5mm [color="Yellow (595nm)" package="5 mm [THT]"]
  Componente8 = Arduino Nano (Rev3.0)
  LCM1602_IIC2 = LCM1602 IIC [part_number="LCM1602 IIC" chip_label="LCM1602 IIC" package="DIP (Dual Inline) [THT]"]
  LCD2 = LCD screen

nets:
  N1: LED10.cathode, LED11.cathode
  N2: LED10.anode, R18.Pin_0
  N3: R17.Pin_0, LED11.anode
  N4: R17.Pin_1, Componente8.D4
  N5: R18.Pin_1, Componente8.D3
  5V: M5.pin1, R19.CW, Componente8.5V, LCM1602_IIC2.VCC
  N6: M5.pin2, R19.CCW, Componente8.GND
  N7: M5.pin3, Componente8.D10
  N8: M5.pin4, Componente8.D12/MISO
  N9: M5.pin5, Componente8.D11/MOSI
  N10: M5.pin6, Componente8.D13/SCK
  N11: M5.pin7, Componente8.D2
  N12: M5.pin8, M5.pin9
  N13: R19.WIPER, Componente8.A0
  N14: Componente8.A5, LCM1602_IIC2.SCL
  N15: Componente8.A4, LCM1602_IIC2.SDA
  VSS: LCM1602_IIC2.VSS, LCD2.VSS
  VDD: LCM1602_IIC2.VDD, LCD2.VDD
  N16: LCM1602_IIC2.V0, LCD2.V0
  N17: LCM1602_IIC2.RS, LCD2.RS
  N18: LCM1602_IIC2.RW, LCD2.R/W
  N19: LCM1602_IIC2.E, LCD2.E
  N20: LCM1602_IIC2.D0, LCD2.DB0
  N21: LCM1602_IIC2.D1, LCD2.DB1
  N22: LCM1602_IIC2.D2, LCD2.DB2
  N23: LCM1602_IIC2.D3, LCD2.DB3
  N24: LCM1602_IIC2.D4, LCD2.DB4
  N25: LCM1602_IIC2.D5, LCD2.DB5
  N26: LCM1602_IIC2.D6, LCD2.DB6
  N27: LCM1602_IIC2.D7, LCD2.DB7
  N28: LCM1602_IIC2.A, LCD2.LED+
  N29: LCM1602_IIC2.K, LCD2.LED-
  N30: LCM1602_IIC2.LED_A, LCM1602_IIC2.LED_B

custom parts:
  Niren can bus module: Niren can bus module availabe on ebay and others. Pcb view assumes that you unsolder the 7 pin header and resolder it on the bottom of the module to connect to the pcb. The two jumpers and the can bus connector remain on the top of the board and don't appear in pcb view.
  LCM1602 IIC: I2C-Module to use a 1602 or 2004 LCD on with the wire.h libory Serial LCD Modul
