# Fritzing sketch node3 (saved by Fritzing 0.9.3b)

parts:
  Componente9 = Arduino Uno (Rev3)
  M6 = Niren can bus module [package=THT]

nets:
  N1: Componente9.D10_PWM/SS, M6.pin3
  N2: Componente9.D11_PWM/MOSI, M6.pin5
  N3: Componente9.D12/MISO, M6.pin4
  N4: Componente9.D13/SCK, M6.pin6
  N5: Componente9.D2, M6.pin7
  N6: Componente9.5V, M6.pin1
  N7: Componente9.GND, M6.pin2
  N8: M6.pin8, M6.pin9

custom parts:
  Niren can bus module: Niren can bus module availabe on ebay and others. Pcb view assumes that you unsolder the 7 pin header and resolder it on the bottom of the module to connect to the pcb. The two jumpers and the can bus connector remain on the top of the board and don't appear in pcb view.
